// Logisim project lab1_logisim_intro.circ as structural Verilog: 8 circuits, main circuit LED计数电路
module \自定义与门  (
);

  wire switch_1_p2, switch_2_p2;

  // Switch #(.width(1)) switch_1: pin names not known; wires that end beside it: 1'b1, switch_1_p2
  // Switch #(.width(1)) switch_2: pin names not known; wires that end beside it: switch_1_p2, switch_2_p2
  LED #(.active("true")) led_1 (.in(switch_2_p2));
endmodule

module \LED计数电路  (
  input  in1,
  input  in2,
  input  in3,
  input  in4,
  input  in5,
  output out1,
  output out2,
  output out3,
  output out4,
  output out5
);

  or or_1 (out1, in1, in2, in3, in4, in5);
  or or_2 (out2, in2, in3, in4, in5);
  or or_3 (out3, in3, in4, in5);
  or or_4 (out4, in4, in5);

  assign out5 = in5;
endmodule

module \LED计数电路测试  (
);

  wire _1_out, _2_out, _3_out, _4_out, _5_out, \LED计数_out1 , \LED计数_out2 , \LED计数_out3 , \LED计数_out4 ,
       \LED计数_out5 ;

  Button _1 (.out(_1_out));
  Button _2 (.out(_2_out));
  Button _3 (.out(_3_out));
  Button _4 (.out(_4_out));
  Button _5 (.out(_5_out));
  \LED计数电路  \LED计数  (
    .in1(_1_out), .in2(_2_out), .in3(_3_out), .in4(_4_out), .in5(_5_out), .out1(\LED计数_out1 ),
    .out2(\LED计数_out2 ), .out3(\LED计数_out3 ), .out4(\LED计数_out4 ), .out5(\LED计数_out5 ));
  LED #(.active("true")) led_1 (.in(\LED计数_out1 ));
  LED #(.active("true")) led_2 (.in(\LED计数_out2 ));
  LED #(.active("true")) led_3 (.in(\LED计数_out3 ));
  LED #(.active("true")) led_4 (.in(\LED计数_out4 ));
  LED #(.active("true")) led_5 (.in(\LED计数_out5 ));
endmodule

module \_5输入编码电路  (
  input  In1,
  input  In2,
  input  In3,
  input  In4,
  input  In5,
  output Out1,
  output Out2,
  output Out3
);

  wire and_1_out, and_2_out, and_3_out, and_4_out, and_5_out, not_1_out, not_2_out, not_3_out, not_4_out,
       not_5_out, not_6_out, not_7_out, not_8_out, not_9_out;

  not not_1 (not_1_out, In4);
  not not_2 (not_2_out, In2);
  not not_3 (not_3_out, In4);
  not not_4 (not_4_out, In4);
  not not_5 (not_5_out, In5);
  not not_6 (not_6_out, In3);
  not not_7 (not_7_out, In4);
  not not_8 (not_8_out, In5);
  not not_9 (not_9_out, In5);
  and and_1 (and_1_out, In3, not_1_out);
  and and_2 (and_2_out, In1, not_2_out, not_3_out);
  and and_3 (and_3_out, In3, not_4_out, not_5_out);
  and and_4 (and_4_out, In2, not_6_out, not_7_out, not_8_out);
  and and_5 (and_5_out, In4, not_9_out);
  or or_1 (Out1, In5, and_1_out, and_2_out);
  or or_2 (Out2, and_3_out, and_4_out);
  or or_3 (Out3, In5, and_5_out);
endmodule

module \_5输入编码电路测试  (
);

  wire _1_out, _2_out, _3_out, _4_out, _5_out, \LED计数_out1 , \LED计数_out2 , \LED计数_out3 , \LED计数_out4 ,
       \LED计数_out5 ;
  wire [2:0] \n5输入编码电路_1_out1 ;

  Button _1 (.out(_1_out));
  Button _2 (.out(_2_out));
  Button _3 (.out(_3_out));
  Button _4 (.out(_4_out));
  Button _5 (.out(_5_out));
  \LED计数电路  \LED计数  (
    .in1(_1_out), .in2(_2_out), .in3(_3_out), .in4(_4_out), .in5(_5_out), .out1(\LED计数_out1 ),
    .out2(\LED计数_out2 ), .out3(\LED计数_out3 ), .out4(\LED计数_out4 ), .out5(\LED计数_out5 ));
  \_5输入编码电路  \u_5输入编码电路_1  (
    .In1(_1_out), .In2(_2_out), .In3(_3_out), .In4(_4_out), .In5(_5_out), .Out1(\n5输入编码电路_1_out1 [0]),
    .Out2(\n5输入编码电路_1_out1 [1]), .Out3(\n5输入编码电路_1_out1 [2]));
  LED #(.active("true")) led_1 (.in(\LED计数_out1 ));
  LED #(.active("true")) led_2 (.in(\LED计数_out2 ));
  LED #(.active("true")) led_3 (.in(\LED计数_out3 ));
  LED #(.active("true")) led_4 (.in(\LED计数_out4 ));
  LED #(.active("true")) led_5 (.in(\LED计数_out5 ));
  // Probe on \n5输入编码电路_1_out1 
  Hex_Digit_Display hex_digit_display_1 (.value({1'b0, \n5输入编码电路_1_out1 }), .dp(1'b1));

  // Notes on the sheet:
  //   16进制显示
endmodule

module \_7段数码管显示驱动  (
  input  In1,
  input  In2,
  input  In3,
  input  In4,
  output Out1,
  output Out2,
  output Out3,
  output Out4,
  output Out5,
  output Out6,
  output Out7
);

  wire and_1_out, and_2_out, and_3_out, and_4_out, and_5_out, and_6_out, and_7_out, and_8_out, and_9_out,
       and_10_out, and_11_out, and_12_out, and_13_out, and_14_out, and_15_out, and_16_out, not_1_out,
       not_2_out, not_3_out, not_4_out, not_5_out, not_6_out, not_7_out, not_8_out, not_9_out, not_10_out,
       not_11_out, not_12_out, not_13_out, not_14_out, not_15_out, not_16_out, not_17_out, not_18_out,
       not_19_out, not_20_out, not_21_out;

  not not_1 (not_1_out, In2);
  and and_1 (and_1_out, not_1_out, In3);
  not not_2 (not_2_out, In1);
  and and_2 (and_2_out, not_2_out, In2);
  and and_3 (and_3_out, In2, not_3_out);
  not not_3 (not_3_out, In3);
  not not_4 (not_4_out, In1);
  and and_4 (and_4_out, not_4_out, not_5_out);
  not not_5 (not_5_out, In2);
  not not_6 (not_6_out, In1);
  and and_5 (and_5_out, not_6_out, In3);
  not not_7 (not_7_out, In2);
  and and_6 (and_6_out, not_7_out, In3);
  not not_8 (not_8_out, In1);
  and and_7 (and_7_out, not_8_out, not_9_out);
  not not_9 (not_9_out, In3);
  and and_8 (and_8_out, In1, In3);
  not not_10 (not_10_out, In1);
  and and_9 (and_9_out, not_10_out, not_11_out);
  not not_11 (not_11_out, In2);
  not not_12 (not_12_out, In3);
  and and_10 (and_10_out, In1, In2);
  not not_13 (not_13_out, In1);
  and and_11 (and_11_out, not_13_out, not_14_out);
  not not_14 (not_14_out, In3);
  not not_15 (not_15_out, In1);
  and and_12 (and_12_out, not_15_out, In2);
  not not_16 (not_16_out, In1);
  and and_13 (and_13_out, not_16_out, not_17_out);
  not not_17 (not_17_out, In3);
  not not_18 (not_18_out, In1);
  and and_14 (and_14_out, not_18_out, In2);
  and and_15 (and_15_out, In2, not_19_out);
  not not_19 (not_19_out, In3);
  not not_20 (not_20_out, In2);
  and and_16 (and_16_out, In1, not_20_out, In3);
  not not_21 (not_21_out, In2);
  or or_1 (Out1, In4, and_1_out, and_2_out, and_3_out);
  or or_2 (Out2, and_4_out, In4, and_5_out, and_6_out);
  or or_3 (Out3, and_7_out, In4, In2, and_8_out);
  or or_4 (Out4, and_9_out, not_12_out, In4, and_10_out);
  or or_5 (Out5, and_11_out, In4, and_12_out);
  or or_6 (Out6, and_13_out, In4, and_14_out, and_15_out, and_16_out);
  or or_7 (Out7, not_21_out, In4, In3, In1);
endmodule

module \_7段数码管驱动测试  (
);

  wire clock_1_out, \n7段数码管显示驱动_1_out1 , \n7段数码管显示驱动_1_out2 , \n7段数码管显示驱动_1_out3 , \n7段数码管显示驱动_1_out4 ,
       \n7段数码管显示驱动_1_out5 , \n7段数码管显示驱动_1_out6 , \n7段数码管显示驱动_1_out7 ;
  wire [3:0] \计数器_q ;

  Clock #(.highDuration(1), .lowDuration(1)) clock_1 (.out(clock_1_out));
  // Probe on \计数器_q 
  Counter #(.width(4), .max('hf), .ongoal("wrap"), .trigger("rising"), .behavior("new")) \u_计数器  (
    .Q(\计数器_q ), .clk(clock_1_out));  // open: load, D, count, carry, clr, preset, down
  \_7段数码管显示驱动  \u_7段数码管显示驱动_1  (
    .In1(\计数器_q [0]), .Out1(\n7段数码管显示驱动_1_out1 ), .In2(\计数器_q [1]), .In3(\计数器_q [2]), .In4(\计数器_q [3]),
    .Out2(\n7段数码管显示驱动_1_out2 ), .Out3(\n7段数码管显示驱动_1_out3 ), .Out4(\n7段数码管显示驱动_1_out4 ),
    .Out5(\n7段数码管显示驱动_1_out5 ), .Out6(\n7段数码管显示驱动_1_out6 ), .Out7(\n7段数码管显示驱动_1_out7 ));
  _7_Segment_Display #(.active("true")) u_7_segment_display_1 (
    .g(\n7段数码管显示驱动_1_out1 ), .f(\n7段数码管显示驱动_1_out2 ), .a(\n7段数码管显示驱动_1_out3 ), .b(\n7段数码管显示驱动_1_out4 ),
    .e(\n7段数码管显示驱动_1_out5 ), .d(\n7段数码管显示驱动_1_out6 ), .c(\n7段数码管显示驱动_1_out7 ), .dp(1'b1));
endmodule

module \最终集成电路图  (
);

  wire _1_out, _2_out, _3_out, _4_out, _5_out, \LED计数_out1 , \LED计数_out2 , \LED计数_out3 , \LED计数_out4 ,
       \LED计数_out5 , \n7段数码管显示驱动_1_out1 , \n7段数码管显示驱动_1_out2 , \n7段数码管显示驱动_1_out3 , \n7段数码管显示驱动_1_out4 ,
       \n7段数码管显示驱动_1_out5 , \n7段数码管显示驱动_1_out6 , \n7段数码管显示驱动_1_out7 ;
  wire [2:0] \n5输入编码电路_1_out1 ;

  Button _1 (.out(_1_out));
  Button _2 (.out(_2_out));
  Button _3 (.out(_3_out));
  Button _4 (.out(_4_out));
  Button _5 (.out(_5_out));
  \LED计数电路  \LED计数  (
    .in1(_1_out), .in2(_2_out), .in3(_3_out), .in4(_4_out), .in5(_5_out), .out1(\LED计数_out1 ),
    .out2(\LED计数_out2 ), .out3(\LED计数_out3 ), .out4(\LED计数_out4 ), .out5(\LED计数_out5 ));
  \_5输入编码电路  \u_5输入编码电路_1  (
    .In1(_1_out), .In2(_2_out), .In3(_3_out), .In4(_4_out), .In5(_5_out), .Out1(\n5输入编码电路_1_out1 [0]),
    .Out2(\n5输入编码电路_1_out1 [1]), .Out3(\n5输入编码电路_1_out1 [2]));
  LED #(.active("true")) led_1 (.in(\LED计数_out1 ));
  LED #(.active("true")) led_2 (.in(\LED计数_out2 ));
  LED #(.active("true")) led_3 (.in(\LED计数_out3 ));
  LED #(.active("true")) led_4 (.in(\LED计数_out4 ));
  LED #(.active("true")) led_5 (.in(\LED计数_out5 ));
  // Probe on \n5输入编码电路_1_out1 
  Hex_Digit_Display hex_digit_display_1 (.value({1'b0, \n5输入编码电路_1_out1 }), .dp(1'b1));
  \_7段数码管显示驱动  \u_7段数码管显示驱动_1  (
    .In1(\n5输入编码电路_1_out1 [0]), .Out1(\n7段数码管显示驱动_1_out1 ), .In2(\n5输入编码电路_1_out1 [1]),
    .In3(\n5输入编码电路_1_out1 [2]), .In4(1'b0), .Out2(\n7段数码管显示驱动_1_out2 ), .Out3(\n7段数码管显示驱动_1_out3 ),
    .Out4(\n7段数码管显示驱动_1_out4 ), .Out5(\n7段数码管显示驱动_1_out5 ), .Out6(\n7段数码管显示驱动_1_out6 ),
    .Out7(\n7段数码管显示驱动_1_out7 ));
  _7_Segment_Display #(.active("true")) u_7_segment_display_1 (
    .g(\n7段数码管显示驱动_1_out1 ), .f(\n7段数码管显示驱动_1_out2 ), .a(\n7段数码管显示驱动_1_out3 ), .b(\n7段数码管显示驱动_1_out4 ),
    .e(\n7段数码管显示驱动_1_out5 ), .d(\n7段数码管显示驱动_1_out6 ), .c(\n7段数码管显示驱动_1_out7 ), .dp(1'b1));

  // Notes on the sheet:
  //   - dasepli@ECNU
  //   - 2020/07/22
  //   计算机硬件系统设计 LAB1
  //   16进制显示
  //   7段管显示
endmodule
